// Logisim project control-logic.circ as structural Verilog: 1 circuit, main circuit control_logic
module control_logic (
  input  [31:0] Instruction,
  input  BrEq,
  input  BrLt,
  output PCSel,
  output RegWEn,
  output [2:0] ImmSel,
  output BrUn,
  output ASel,
  output BSel,
  output [3:0] ALUSel,
  output MemWEn,
  output [1:0] WBSel
);

  wire add, add_on, addi, and_tun, andi, demultiplexer_3_out0, demultiplexer_3_out1, demultiplexer_4_out5,
       I_IMM_ON, mul, mul_on, mulh, mulh_on, mulhu, or_tun, ori, R_ON, sll_on, sll_tun, slli, slt, slti,
       sra_on, sra_tun, srai, srai_on, srl_on, srl_sra_tun, srl_tun, srli, srli_on, sub, sub_on, xor_tun,
       xori;
  wire [2:0] I_Imm_Func3, R_Func3;
  wire [5:0] priority_encoder_1_out;
  wire [6:0] I_Imm_Funct7, R_Funct7;
  wire [15:14] rom_1_data;
  wire [24:0] demultiplexer_1_out1, demultiplexer_2_out1;

  Comparator #(.width(7)) comparator_1 (.a(Instruction[6:0]), .b(7'b0110011), .eq(R_ON));  // open: gt, lt
  Priority_Encoder #(.select_enc(6)) priority_encoder_1 (
    .in0(add), .in1(mul), .in2(sub), .in3(sll_tun), .in4(mulh), .in5(mulhu), .in6(slt), .in7(xor_tun),
    .in8(srl_tun), .in9(sra_tun), .in10(or_tun), .in11(and_tun), .in15(addi), .in16(slli), .in17(slti),
    .in18(xori), .in19(srli), .in20(srai), .in21(ori), .in22(andi), .out(priority_encoder_1_out));  // open: in12, in13, in14, in23, in24, in25, in26, in27, in28, in29, in30, in31, in32, in33, in34, in35, in36, in37, in38, in39, in40, in41, in42, in43, in44, in45, in46, in47, in48, in49, in50, in51, in52, in53, in54, in55, in56, in57, in58, in59, in60, in61, in62, in63, gs, en_out, en_in
  Comparator #(.width(7)) comparator_2 (.a(Instruction[6:0]), .b(7'b0010011), .eq(I_IMM_ON));  // open: gt, lt
  ROM #(.addrWidth(6), .dataWidth(16)) rom_1 (
    .addr(priority_encoder_1_out),
    .data({rom_1_data, WBSel, MemWEn, ALUSel, BSel, ASel, BrUn, ImmSel, RegWEn}));
  Demultiplexer #(.width(32)) demultiplexer_1 (
    .out1({R_Funct7, demultiplexer_1_out1[24:15], R_Func3, demultiplexer_1_out1[11:0]}), .in(Instruction),
    .sel(R_ON));  // open: out0
  Demultiplexer #(.width(32)) demultiplexer_2 (
    .out1({I_Imm_Funct7, demultiplexer_2_out1[24:15], I_Imm_Func3, demultiplexer_2_out1[11:0]}),
    .in(Instruction), .sel(I_IMM_ON));  // open: out0
  and and_1 (add, add_on, demultiplexer_3_out0);
  Demultiplexer #(.select(3)) demultiplexer_3 (
    .out0(demultiplexer_3_out0), .out1(demultiplexer_3_out1), .out2(slt), .out3(mulhu), .out4(xor_tun),
    .out5(srl_sra_tun), .out6(or_tun), .out7(and_tun), .in(R_ON), .sel(R_Func3));
  Comparator #(.width(7)) comparator_3 (.a(R_Funct7), .b({7{1'b0}}), .eq(add_on));  // open: gt, lt
  Comparator #(.width(7)) comparator_4 (.a(R_Funct7), .b(7'b0100000), .eq(sub_on));  // open: gt, lt
  Comparator #(.width(7)) comparator_5 (.a(R_Funct7), .b(7'b0000001), .eq(mul_on));  // open: gt, lt
  Demultiplexer #(.select(3)) demultiplexer_4 (
    .out0(addi), .out1(slli), .out2(slti), .out4(xori), .out5(demultiplexer_4_out5), .out6(ori), .out7(andi),
    .in(I_IMM_ON), .sel(I_Imm_Func3));  // open: out3
  Comparator #(.width(7)) comparator_6 (.a(I_Imm_Funct7), .b({7{1'b0}}), .eq(srai_on));  // open: gt, lt
  Comparator #(.width(7)) comparator_7 (.a(I_Imm_Funct7), .b(7'b0100000), .eq(srli_on));  // open: gt, lt
  and and_2 (sub, sub_on, demultiplexer_3_out0);
  or or_1 (PCSel, 1'b0, 1'b0);
  and and_3 (srai, srai_on, demultiplexer_4_out5);
  and and_4 (mul, mul_on, demultiplexer_3_out0);
  Comparator #(.width(7)) comparator_8 (.a(R_Funct7), .b({7{1'b0}}), .eq(sll_on));  // open: gt, lt
  Comparator #(.width(7)) comparator_9 (.a(R_Funct7), .b(7'b0000001), .eq(mulh_on));  // open: gt, lt
  and and_5 (srli, srli_on, demultiplexer_4_out5);
  and and_6 (sll_tun, sll_on, demultiplexer_3_out1);
  and and_7 (mulh, mulh_on, demultiplexer_3_out1);
  Comparator #(.width(7)) comparator_10 (.a(R_Funct7), .b({7{1'b0}}), .eq(srl_on));  // open: gt, lt
  Comparator #(.width(7)) comparator_11 (.a(R_Funct7), .b(7'b0100000), .eq(sra_on));  // open: gt, lt
  and and_8 (srl_tun, srl_sra_tun, srl_on);
  and and_9 (sra_tun, srl_sra_tun, sra_on);

  // Notes on the sheet:
  //   INPUTS to your circuit
  //   contents of rom_1 (hex, n*v repeats v):
  //   100f 140f 160f 108f 148f 158f 110f 120f 128f 168f 130f 138f 1841 1841 1841 1041 10c1 1141 1341 12c1
  //   16c1 1341 13c1 9*0 4*1
  //   ROM FOR CONTROL LOGIC
  //   DON'T CHANGE THE LOCATIONS OF THE INPUTS AND OUTPUTS!
  //   This is only if you choose to do the ROM option
  //   OUTPUT from your circuit
  //   Reminder: If using ROM, use combinational logic for PCSel
endmodule
